// Logisim project alu.circ as structural Verilog: 1 circuit, main circuit alu
module alu (
  input  [31:0] A,
  input  [31:0] B,
  input  [3:0] ALUSel,
  input  [3:0] in_4,
  input  [3:0] in_5,
  input  [3:0] in_6,
  input  [3:0] in_7,
  output [31:0] Result,
  output [3:0] out_9,
  output out_10,
  output [2:0] out_11,
  output [3:0] out_12,
  output [2:0] out_13
);

  wire [0:0] slt7;
  wire [30:0] mulh14;
  wire [31:0] add0, and1, divu8, EMPTY, mul10, mulhu11, or2, remu9, sll6, sra5, srl4, sub12, xor3;

  Adder #(.width(32)) adder_1 (.a(A), .b(B), .out(add0));  // open: cin, cout
  assign and1 = A & B;  // AND_Gate and_1, 32 bits wide
  assign or2 = A | B;  // OR_Gate or_1, 32 bits wide
  assign xor3 = A ^ B;  // XOR_Gate xor_1, 32 bits wide
  Shifter #(.width(32), .shift("lr")) shifter_1 (.in(A), .\dist (B[4:0]), .out(srl4));
  Shifter #(.width(32), .shift("ar")) shifter_2 (.in(A), .\dist (B[4:0]), .out(sra5));
  Shifter #(.width(32)) shifter_3 (.in(A), .\dist (B[4:0]), .out(sll6));
  Comparator #(.width(32)) comparator_1 (.a(A), .b(B), .lt(slt7[0]));  // open: gt, eq
  Divider #(.width(32)) divider_1 (.a(A), .b(B), .out(divu8));  // open: upper, rem
  Divider #(.width(32)) divider_2 (.a(A), .b(B), .rem(remu9));  // open: out, upper
  Multiplier #(.width(32)) multiplier_1 (.a(A), .b(B), .cout(mulhu11));  // open: out, cin
  Subtractor #(.width(32)) subtractor_1 (.a(A), .b(B), .out(sub12));  // open: bin, bout
  xor xor_2 (mul10[31], A[31], B[31]);
  Multiplier #(.width(31)) multiplier_2 (.a(A[30:0]), .b(B[30:0]), .out(mul10[30:0]));  // open: cin, cout
  // XOR_Gate xor_3 has open pins: in0=A[31], in1=B[31], out=open
  Multiplier #(.width(31)) multiplier_3 (.a(A[30:0]), .b(B[30:0]), .cout(mulh14));  // open: out, cin
  Comparator #(.width(4)) comparator_2 (.a(in_4), .b(in_5), .lt(out_9[0]));  // open: gt, eq
  xor xor_4 (out_10, in_6[3], in_7[3]);
  Multiplier #(.width(3)) multiplier_4 (.a(in_6[2:0]), .b(in_7[2:0]), .out(out_11), .cout(out_12[2:0]));  // open: cin
  Multiplexer #(.select(4), .width(32), .enable("false")) multiplexer_1 (
    .in0(add0), .in1(and1), .in2(or2), .in3(xor3), .in4(srl4), .in5(sra5), .in6(sll6),
    .in7({{31{1'b0}}, slt7[0]}), .in8(divu8), .in9(remu9), .in10(mul10), .in11(mulhu11), .in12(sub12),
    .in13(B), .in14({1'b0, mulh14}), .in15(EMPTY), .out(Result), .sel(ALUSel));

  assign out_9[3:1] = 3'b000;
  assign out_12[3] = 1'b0;
  assign out_13 = out_12[2:0];

  // Other names for the same wires on the sheet: bsel13[31:0] = B

  // Notes on the sheet:
  //   INPUTS to your circuit
  //   DON'T CHANGE THE LOCATIONS OF THE INPUTS AND OUTPUTS!
  //   OUTPUT from your circuit
endmodule
