// Logisim project branch_comp.circ as structural Verilog: 1 circuit, main circuit branch_comp
module branch_comp (
  input  [31:0] rs1,
  input  [31:0] rs2,
  input  BrUn,
  output BrEq,
  output BrLt,
  output out_6
);

  wire [31:0] signed_rs1, signed_rs2, unsigned_rs1, unsigned_rs2;

  Demultiplexer #(.width(32), .enable("false")) demultiplexer_1 (
    .out0(signed_rs1), .out1(unsigned_rs1), .in(rs1), .sel(BrUn));
  Demultiplexer #(.width(32), .enable("false")) demultiplexer_2 (
    .out0(signed_rs2), .out1(unsigned_rs2), .in(rs2), .sel(BrUn));
  Comparator #(.width(32)) comparator_1 (.a(signed_rs1), .b(signed_rs2), .gt(out_6), .eq(BrEq), .lt(BrLt));
  Comparator #(.width(32), .mode("unsigned")) comparator_2 (
    .a(unsigned_rs1), .b(unsigned_rs2), .eq(BrEq), .lt(BrLt));  // open: gt

  // Notes on the sheet:
  //   INPUTS to your circuit
  //   DON'T CHANGE THE LOCATIONS OF THE INPUTS AND OUTPUTS!
  //   OUTPUT from your circuit
endmodule
