// Logisim project control_logic.circ as structural Verilog: 1 circuit, main circuit control_logic
module control_logic (
  input  [31:0] inst,
  input  BrEq,
  input  BrLt,
  output PCSel,
  output RegWEn,
  output [2:0] ImmSel,
  output BrUn,
  output ASel,
  output BSel,
  output [3:0] ALUSel,
  output MemRW,
  output [1:0] WBSel
);

  wire and_1_out, and_2_out, and_3_out, and_4_out, and_5_out, and_6_out, and_7_out, and_8_out, and_9_out,
       and_10_out, and_11_out, and_12_out, and_13_out, and_14_out, and_15_out, and_16_out, and_17_out,
       and_18_out, and_19_out, and_20_out, and_21_out, and_22_out, and_23_out, and_24_out, and_25_out,
       and_26_out, and_27_out, and_28_out, and_29_out, func3_is_0, func3_is_1, func3_is_2, func3_is_3,
       func3_is_4, func3_is_5, func3_is_6, func3_is_7, func7_is_00, func7_is_01, func7_is_20, is_I_format,
       is_I_format_jalr, is_I_format_lblhlw, is_R_format, is_S_format, is_SB_format, is_U_format_auipc,
       is_U_format_lui, is_UJ_format, not_1_out, not_2_out, not_3_out, not_4_out, or_1_out, or_2_out,
       or_3_out, or_4_out, or_5_out, or_6_out, or_7_out, or_8_out, or_9_out, or_10_out, or_11_out, or_12_out,
       or_13_out, or_14_out, or_15_out, or_16_out, or_17_out;

  Comparator #(.width(7), .mode("unsigned")) comparator_1 (
    .a(inst[6:0]), .b(7'b1100011), .eq(is_SB_format));  // open: gt, lt
  Comparator #(.width(7), .mode("unsigned")) comparator_2 (
    .a(inst[6:0]), .b(7'b1100111), .eq(is_I_format_jalr));  // open: gt, lt
  Comparator #(.width(7), .mode("unsigned")) comparator_3 (
    .a(inst[6:0]), .b(7'b1101111), .eq(is_UJ_format));  // open: gt, lt
  Comparator #(.width(7), .mode("unsigned")) comparator_4 (
    .a(inst[6:0]), .b(7'b0110011), .eq(is_R_format));  // open: gt, lt
  Comparator #(.width(7), .mode("unsigned")) comparator_5 (
    .a(inst[6:0]), .b(7'b0000011), .eq(is_I_format_lblhlw));  // open: gt, lt
  Comparator #(.width(7), .mode("unsigned")) comparator_6 (
    .a(inst[6:0]), .b(7'b0010011), .eq(is_I_format));  // open: gt, lt
  Comparator #(.width(7), .mode("unsigned")) comparator_7 (
    .a(inst[6:0]), .b(7'b0100011), .eq(is_S_format));  // open: gt, lt
  Comparator #(.width(7), .mode("unsigned")) comparator_8 (
    .a(inst[6:0]), .b(7'b0010111), .eq(is_U_format_auipc));  // open: gt, lt
  Comparator #(.width(7), .mode("unsigned")) comparator_9 (
    .a(inst[6:0]), .b(7'b0110111), .eq(is_U_format_lui));  // open: gt, lt
  Comparator #(.width(3), .mode("unsigned")) comparator_10 (
    .a(inst[14:12]), .b(3'b000), .eq(func3_is_0));  // open: gt, lt
  Comparator #(.width(3), .mode("unsigned")) comparator_11 (
    .a(inst[14:12]), .b(3'b001), .eq(func3_is_1));  // open: gt, lt
  Comparator #(.width(3), .mode("unsigned")) comparator_12 (
    .a(inst[14:12]), .b(3'b010), .eq(func3_is_2));  // open: gt, lt
  Comparator #(.width(3), .mode("unsigned")) comparator_13 (
    .a(inst[14:12]), .b(3'b011), .eq(func3_is_3));  // open: gt, lt
  Comparator #(.width(3), .mode("unsigned")) comparator_14 (
    .a(inst[14:12]), .b(3'b100), .eq(func3_is_4));  // open: gt, lt
  Comparator #(.width(3), .mode("unsigned")) comparator_15 (
    .a(inst[14:12]), .b(3'b101), .eq(func3_is_5));  // open: gt, lt
  Comparator #(.width(3), .mode("unsigned")) comparator_16 (
    .a(inst[14:12]), .b(3'b110), .eq(func3_is_6));  // open: gt, lt
  Comparator #(.width(3), .mode("unsigned")) comparator_17 (
    .a(inst[14:12]), .b(3'b111), .eq(func3_is_7));  // open: gt, lt
  Comparator #(.width(7), .mode("unsigned")) comparator_18 (
    .a(inst[31:25]), .b({7{1'b0}}), .eq(func7_is_00));  // open: gt, lt
  Comparator #(.width(7), .mode("unsigned")) comparator_19 (
    .a(inst[31:25]), .b(7'b0000001), .eq(func7_is_01));  // open: gt, lt
  Comparator #(.width(7), .mode("unsigned")) comparator_20 (
    .a(inst[31:25]), .b(7'b0100000), .eq(func7_is_20));  // open: gt, lt
  and and_1 (and_1_out, is_I_format, func3_is_0);
  and and_2 (and_2_out, func3_is_0, is_R_format, func7_is_00);
  and and_3 (and_3_out, func3_is_0, is_R_format, func7_is_01);
  and and_4 (and_4_out, func3_is_0, is_R_format, func7_is_20);
  and and_5 (and_5_out, func3_is_1, is_R_format, func7_is_00);
  and and_6 (and_6_out, func3_is_1, is_I_format, func7_is_00);
  and and_7 (and_7_out, func3_is_1, is_R_format, func7_is_01);
  and and_8 (and_8_out, func3_is_3, is_R_format, func7_is_00);
  and and_9 (and_9_out, is_I_format, func3_is_2);
  and and_10 (and_10_out, func3_is_2, is_R_format, func7_is_00);
  and and_11 (and_11_out, is_I_format, func3_is_4);
  and and_12 (and_12_out, func3_is_4, is_R_format, func7_is_00);
  or or_1 (or_1_out, and_1_out, and_2_out);
  Multiplexer #(.width(4), .enable("false")) multiplexer_1 (.in1(4'b1010), .out(ALUSel), .sel(and_3_out));  // open: in0
  Multiplexer #(.width(4), .enable("false")) multiplexer_2 (.in1(4'b1100), .out(ALUSel), .sel(and_4_out));  // open: in0
  or or_2 (or_2_out, and_5_out, and_6_out);
  Multiplexer #(.width(4), .enable("false")) multiplexer_3 (.in1(4'b1110), .out(ALUSel), .sel(and_7_out));  // open: in0
  Multiplexer #(.width(4), .enable("false")) multiplexer_4 (.in1(4'b1011), .out(ALUSel), .sel(and_8_out));  // open: in0
  or or_3 (or_3_out, and_9_out, and_10_out);
  or or_4 (or_4_out, and_11_out, and_12_out);
  Multiplexer #(.width(4), .enable("false")) multiplexer_5 (.in1(4'b0000), .out(ALUSel), .sel(or_1_out));  // open: in0
  Multiplexer #(.width(4), .enable("false")) multiplexer_6 (.in1(4'b0110), .out(ALUSel), .sel(or_2_out));  // open: in0
  Multiplexer #(.width(4), .enable("false")) multiplexer_7 (.in1(4'b0111), .out(ALUSel), .sel(or_3_out));  // open: in0
  Multiplexer #(.width(4), .enable("false")) multiplexer_8 (.in1(4'b0011), .out(ALUSel), .sel(or_4_out));  // open: in0
  and and_13 (and_13_out, func3_is_5, is_I_format, func7_is_00);
  and and_14 (and_14_out, func3_is_5, is_R_format, func7_is_00);
  and and_15 (and_15_out, func3_is_5, is_R_format, func7_is_20);
  and and_16 (and_16_out, func3_is_5, is_I_format, func7_is_20);
  and and_17 (and_17_out, is_I_format, func3_is_6);
  and and_18 (and_18_out, func3_is_6, is_R_format, func7_is_00);
  Multiplexer #(.width(4), .enable("false")) multiplexer_9 (
    .in1(4'b1000), .out(ALUSel), .sel(and_19_out));  // open: in0
  and and_19 (and_19_out, func3_is_5, is_R_format, func7_is_01);
  or or_5 (or_5_out, and_13_out, and_14_out);
  or or_6 (or_6_out, and_15_out, and_16_out);
  and and_20 (and_20_out, is_I_format, func3_is_7);
  and and_21 (and_21_out, func3_is_7, is_R_format, func7_is_01);
  and and_22 (and_22_out, func3_is_7, is_R_format, func7_is_00);
  Multiplexer #(.width(4), .enable("false")) multiplexer_10 (.in1(4'b0100), .out(ALUSel), .sel(or_5_out));  // open: in0
  Multiplexer #(.width(4), .enable("false")) multiplexer_11 (.in1(4'b0101), .out(ALUSel), .sel(or_6_out));  // open: in0
  or or_7 (or_7_out, and_17_out, and_18_out);
  or or_8 (or_8_out, and_20_out, and_21_out);
  Multiplexer #(.width(4), .enable("false")) multiplexer_12 (
    .in1(4'b0001), .out(ALUSel), .sel(and_22_out));  // open: in0
  Multiplexer #(.width(4), .enable("false")) multiplexer_13 (.in1(4'b0010), .out(ALUSel), .sel(or_7_out));  // open: in0
  Multiplexer #(.width(4), .enable("false")) multiplexer_14 (.in1(4'b1001), .out(ALUSel), .sel(or_8_out));  // open: in0
  or or_9 (or_9_out, is_SB_format, is_I_format_jalr, is_UJ_format, is_I_format_lblhlw, is_S_format);
  or or_10 (or_10_out, is_U_format_auipc, is_U_format_lui);
  Multiplexer #(.width(4), .enable("false")) multiplexer_15 (.in1(4'b0000), .out(ALUSel), .sel(or_9_out));  // open: in0
  Multiplexer #(.width(4), .enable("false")) multiplexer_16 (
    .in1(4'b1101), .out(ALUSel), .sel(or_10_out));  // open: in0
  not not_1 (not_1_out, BrEq);
  and and_23 (and_23_out, func3_is_1, is_SB_format, not_1_out);
  Multiplexer #(.enable("false")) multiplexer_17 (.in1(1'b1), .out(PCSel));  // open: in0, sel
  not not_2 (not_2_out, BrEq);
  Multiplexer #(.enable("false")) multiplexer_18 (.in0(1'b0), .in1(1'b1), .out(MemRW), .sel(is_S_format));
  or or_11 (or_11_out, is_S_format, is_SB_format);
  or or_12 (or_12_out, is_I_format_jalr, is_UJ_format);
  or or_13 (or_13_out, is_R_format, is_I_format, is_U_format_auipc, is_U_format_lui);
  not not_3 (not_3_out, func3_is_0);
  not not_4 (not_4_out, func3_is_1);
  Multiplexer #(.enable("false")) multiplexer_19 (.in0(1'b1), .in1(1'b0), .out(RegWEn), .sel(or_11_out));
  Multiplexer #(.width(2), .enable("false")) multiplexer_20 (.in1(2'b00), .out(WBSel), .sel(or_12_out));  // open: in0
  Multiplexer #(.width(2), .enable("false")) multiplexer_21 (.in1(2'b01), .out(WBSel), .sel(or_13_out));  // open: in0
  Multiplexer #(.width(2), .enable("false")) multiplexer_22 (
    .in1(2'b10), .out(WBSel), .sel(is_I_format_lblhlw));  // open: in0
  and and_24 (and_24_out, is_SB_format, not_3_out, not_4_out);
  and and_25 (and_25_out, func3_is_1, is_SB_format, not_2_out);
  and and_26 (and_26_out, func3_is_0, is_SB_format, BrEq);
  Multiplexer #(.enable("false")) multiplexer_23 (.in0(1'b0), .in1(1'b1), .out(PCSel), .sel(or_14_out));
  or or_14 (or_14_out, and_24_out, is_I_format_jalr, is_UJ_format, and_25_out, and_26_out);
  and and_27 (and_27_out, func3_is_0, is_SB_format, BrEq);
  Multiplexer #(.enable("false")) multiplexer_24 (.in1(1'b1), .out(PCSel));  // open: in0, sel
  or or_15 (or_15_out, is_SB_format, is_UJ_format, is_U_format_auipc);
  Multiplexer #(.width(3), .enable("false")) multiplexer_25 (.in1(3'b000), .out(ImmSel), .sel(or_16_out));  // open: in0
  or or_16 (or_16_out, is_I_format_jalr, is_I_format);
  or or_17 (or_17_out, is_U_format_auipc, is_U_format_lui);
  Multiplexer #(.enable("false")) multiplexer_26 (.in0(1'b0), .in1(1'b1), .out(ASel), .sel(or_15_out));
  Multiplexer #(.enable("false")) multiplexer_27 (.in0(1'b1), .in1(1'b0), .out(BSel), .sel(is_R_format));
  and and_28 (and_28_out, is_SB_format, func3_is_4);
  and and_29 (and_29_out, func3_is_6, is_SB_format);
  Multiplexer #(.width(3), .enable("false")) multiplexer_28 (
    .in1(3'b001), .out(ImmSel), .sel(is_S_format));  // open: in0
  Multiplexer #(.width(3), .enable("false")) multiplexer_29 (
    .in1(3'b010), .out(ImmSel), .sel(is_SB_format));  // open: in0
  Multiplexer #(.width(3), .enable("false")) multiplexer_30 (.in1(3'b011), .out(ImmSel), .sel(or_17_out));  // open: in0
  Multiplexer #(.width(3), .enable("false")) multiplexer_31 (
    .in1(3'b100), .out(ImmSel), .sel(is_UJ_format));  // open: in0
  Demultiplexer #(.enable("false")) demultiplexer_1 (.out1(BrUn), .in(1'b0), .sel(and_28_out));  // open: out0
  Demultiplexer #(.enable("false")) demultiplexer_2 (.out1(BrUn), .in(1'b1), .sel(and_29_out));  // open: out0

  // Other names for the same wires on the sheet: opcode[6:0] = inst[6:0]; func3[2:0] = inst[14:12];
  //   func7[6:0] = inst[31:25]

  // Notes on the sheet:
  //   INPUTS to your circuit
  //   DON'T CHANGE THE LOCATIONS OF THE INPUTS AND OUTPUTS!
  //   OUTPUT from your circuit
  //   Except S and SB format, all formats need to set RegWen as 1(Y)
  //   If it is SB format and it is not beq or bne, set PCSel as 1
  //   Default value is 0(read), because we do not want to accidently write in to memory
endmodule
