// Logisim project cpu.circ as structural Verilog: 1 circuit, main circuit main
module main (
  input  [31:0] INSTRUCTION,
  input  CLOCK,
  output [31:0] PROGRAM_COUNTER,
  output [31:0] ra,
  output [31:0] sp,
  output [31:0] t0,
  output [31:0] t1,
  output [31:0] t2,
  output [31:0] s0,
  output [31:0] s1,
  output [31:0] a0
);

  wire and_3_out, ASel, BrEq, BrLt, BrUn, BSel, comparator_4_eq, comparator_5_eq, func3_is_0, func3_is_1,
       is_SB_format, MemRW, not_1_out, or_1_out, or_2_out, PCSel, RegWEn;
  wire [1:0] WBSel;
  wire [2:0] ImmSel;
  wire [3:0] ALUSel;
  wire [31:0] adder_1_out, adder_2_out, alu_output_normal, check_if_it_is_branch, imm_output, mem_output,
       multiplexer_1_out, multiplexer_2_out, multiplexer_3_out, multiplexer_4_out, pc_pipeline, rs1_output,
       rs2_output, wb_value;

  Adder #(.width(32)) adder_1 (.a(PROGRAM_COUNTER), .b(32'h4), .out(adder_1_out));  // open: cin, cout
  not not_1 (not_1_out, BrEq);
  Multiplexer #(.width(32), .enable("false")) multiplexer_1 (
    .in0(adder_1_out), .in1(alu_output_normal), .out(multiplexer_1_out), .sel(PCSel));
  // AND_Gate and_1 has open pins: in0=is_SB_format, in1=func3_is_1, in2=not_1_out, out=open
  // AND_Gate and_2 has open pins: in0=is_SB_format, in1=func3_is_0, in2=BrEq, out=open
  Register #(.width(32)) PC (.D(multiplexer_1_out), .clk(CLOCK), .Q(PROGRAM_COUNTER));  // open: en, clr
  Comparator #(.width(7), .mode("unsigned")) comparator_1 (
    .a(check_if_it_is_branch[6:0]), .b(7'b1100011), .eq(is_SB_format));  // open: gt, lt
  Comparator #(.width(3), .mode("unsigned")) comparator_2 (
    .a(check_if_it_is_branch[14:12]), .b(3'b000), .eq(func3_is_0));  // open: gt, lt
  Comparator #(.width(3), .mode("unsigned")) comparator_3 (
    .a(check_if_it_is_branch[14:12]), .b(3'b001), .eq(func3_is_1));  // open: gt, lt
  control_logic control_logic_1 (
    .BSel(BSel), .ASel(ASel), .BrUn(BrUn), .ImmSel(ImmSel), .RegWEn(RegWEn), .PCSel(PCSel), .BrLt(BrLt),
    .BrEq(BrEq), .inst(check_if_it_is_branch), .ALUSel(ALUSel), .MemRW(MemRW), .WBSel(WBSel));
  Multiplexer #(.width(32), .enable("false")) multiplexer_2 (
    .in0(INSTRUCTION), .in1(32'h13), .out(multiplexer_2_out), .sel(or_2_out));
  Register #(.width(32)) register_1 (.D(PROGRAM_COUNTER), .clk(CLOCK), .Q(pc_pipeline));  // open: en, clr
  Register #(.width(32)) register_2 (.D(multiplexer_2_out), .clk(CLOCK), .Q(check_if_it_is_branch));  // open: en, clr
  Comparator #(.width(7), .mode("unsigned")) comparator_4 (
    .a(check_if_it_is_branch[6:0]), .b(7'b1101111), .eq(comparator_4_eq));  // open: gt, lt
  Comparator #(.width(7), .mode("unsigned")) comparator_5 (
    .a(check_if_it_is_branch[6:0]), .b(7'b1100111), .eq(comparator_5_eq));  // open: gt, lt
  and and_3 (and_3_out, PCSel, is_SB_format);
  or or_1 (or_1_out, comparator_4_eq, comparator_5_eq);
  or or_2 (or_2_out, or_1_out, and_3_out);
  imm_gen imm_gen_1 (.ImmSel(ImmSel), .inst(check_if_it_is_branch), .imm(imm_output));
  regfile_main RegFile (
    .rs2(check_if_it_is_branch[24:20]), .rd(check_if_it_is_branch[11:7]), .Read_Data_1(rs1_output),
    .Read_Data_2(rs2_output), .ra(ra), .sp(sp), .t0(t0), .t1(t1), .t2(t2), .s0(s0), .s1(s1), .a0(a0),
    .rs1(check_if_it_is_branch[19:15]), .Write_Data(wb_value), .RegWEn(RegWEn), .clk(CLOCK));
  branch_comp branch_comp_1 (.BrEq(BrEq), .rs1(rs1_output), .rs2(rs2_output), .BrLt(BrLt), .BrUn(BrUn));  // open: out_6
  Multiplexer #(.width(32), .enable("false")) multiplexer_3 (
    .in0(rs1_output), .in1(pc_pipeline), .out(multiplexer_3_out), .sel(ASel));
  Multiplexer #(.width(32), .enable("false")) multiplexer_4 (
    .in0(rs2_output), .in1(imm_output), .out(multiplexer_4_out), .sel(BSel));
  alu Arithmetic_Logic_Unit (.Result(alu_output_normal), .ALUSel(ALUSel), .A(multiplexer_3_out), .B(multiplexer_4_out));
  // mem_main DMEM: pin names not known; wires that end beside it: alu_output_normal, rs2_output, CLOCK, MemRW, mem_output
  Adder #(.width(32)) adder_2 (.a(32'h4), .b(pc_pipeline), .out(adder_2_out));  // open: cin, cout
  Multiplexer #(.select(2), .width(32), .enable("false")) multiplexer_5 (
    .in0(adder_2_out), .in1(alu_output_normal), .in2(mem_output), .out(wb_value), .sel(WBSel));  // open: in3

  // Other names for the same wires on the sheet: alu_output_pc[31:0] = alu_output_normal; clk = CLOCK;
  //   fetch_addr[31:0] = PROGRAM_COUNTER; check_if_it_is_jump[31:0] = check_if_it_is_branch;
  //   inst_pipeline[31:0] = check_if_it_is_branch; rd[4:0] = check_if_it_is_branch[11:7];
  //   rs1[4:0] = check_if_it_is_branch[19:15]; rs2[4:0] = check_if_it_is_branch[24:20]

  // Notes on the sheet:
  //   if it is bne is taken
  //   if it is beq is taken
  //   Output
  //   IF Stage
  //   output from IMEM in run.circ
  //   IMEM (do **NOT** move this)
  //   input to IMEM in run.circ
  //   Inputs
  //   nop
  //   if PCSel==1(ALU), means branch is taken
  //   It is OK to move the PC, RegFile, ALU, MEM, Branch Comp, Imm Gen, and Control Logic to wherever is most convenient for you when constructing your CPU, and to delete this text
  //   Inputs/Outputs for testing. Do **NOT** move these.
  //   ID Stage
  //   TODO: if func3 is 0, igonre 1 bit
endmodule
