// Logisim project imm_gen.circ as structural Verilog: 1 circuit, main circuit imm_gen
module imm_gen (
  input  [31:0] inst,
  input  [2:0] ImmSel,
  output [31:0] imm
);

  wire [31:11] I_format, S_format;
  wire [31:12] SB_format;
  wire [31:20] UJ_format;

  assign I_format = {{20{inst[31]}}, inst[31]};  // Bit_Extender bit_extender_1
  assign S_format = {{20{inst[31]}}, inst[31]};  // Bit_Extender bit_extender_2
  assign SB_format = {{19{inst[31]}}, inst[31]};  // Bit_Extender bit_extender_3
  assign UJ_format = {{11{inst[31]}}, inst[31]};  // Bit_Extender bit_extender_4
  Multiplexer #(.select(3), .width(32), .enable("false")) multiplexer_1 (
    .in0({I_format, inst[30:20]}), .in1({S_format, inst[30:25], inst[11:7]}),
    .in2({SB_format, inst[7], inst[30:25], inst[11:8], 1'b0}), .in3({inst[31:12], {12{1'b0}}}),
    .in4({UJ_format, inst[19:12], inst[20], inst[30:21], 1'b0}), .out(imm), .sel(ImmSel));  // open: in5, in6, in7

  // Other names for the same wires on the sheet: S_format[10:0] = {inst[30:25], inst[11:7]};
  //   SB_format[11:1] = {inst[7], inst[30:25], inst[11:8]}; U_format[31:12] = inst[31:12];
  //   I_format[10:0] = inst[30:20]; UJ_format[19:1] = {inst[19:12], inst[20], inst[30:21]}

  // Notes on the sheet:
  //   INPUTS to your circuit
  //   DON'T CHANGE THE LOCATIONS OF THE INPUTS AND OUTPUTS!
  //   OUTPUT from your circuit
endmodule
